# Fritzing sketch fritzing_diagram (saved by Fritzing 0.9.4)
breadboards: 1

parts:
  Mod1 = Arduino Uno WIFI REV2
  LCD2004-I2C1 = LCD2004-I2C
  Part1 = 24 NeoPixel Ring [part_number=1586]

nets:
  5V: Mod1.5V, Part1.VDD
  GND: Mod1.GND, Part1.GND
  N1: Mod1.D12/MISO, Part1.IN
  N2: Mod1.A4/SDA, LCD2004-I2C1.SDA
  N3: Mod1.A5/SCL, LCD2004-I2C1.SCL

custom parts:
  Arduino Uno WIFI REV2: The Arduino Uno WIFI REV2 is a microcontroller board based on the ATmega 4809. It has 14 digital input/output pins (of which 5 can be used as PWM outputs), 6 analog inputs, a 16 MHz ceramic resonator, a USB connection, a power jack, an ICSP header, and a reset button. It also has a WIFI controller with a secure ECC608 crypto unit and an internal IMU. It contains everything needed to support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
  LCD2004-I2C: A standard character display with 4x20 characters. Comes in many colors with LCM2004 IIC attached.
  24 NeoPixel Ring: 24 ultra bright smart LED NeoPixels are arranged in a circle with 2.6" (66mm) outer diameter. The rings are 'chainable' - connect the output pin of one to the input pin of another. Use only one microcontroller pin to control as many as you can chain together! Each LED is addressable as the driver chip is inside the LED. Each one has ~18mA constant current drive so the color will be very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
